# Fritzing sketch blink_led (saved by Fritzing 0.9.0b)
circuit board: 4.61846cm x 3.11744cm
breadboards: 1

parts:
  Raspberry_Pi = Raspberry Pi B rev2
  R1 = Resistor [tolerance=±5% resistance=1k package=THT]
  LED1 = LED - 5mm [color="Red (633nm)" package="5 mm [THT]"]

nets:
  N1: Raspberry_Pi.GND, R1.Pin_0
  N2: Raspberry_Pi.GPIO_17, LED1.anode
  N3: R1.Pin_1, LED1.cathode
